// Logisim project DigitalClock2-0.circ as structural Verilog
// SevenBit
module sevenbit (
  input  D3,
  input  D2,
  input  D1,
  input  D0,
  output out_5,
  output out_6,
  output out_7,
  output out_8,
  output out_9,
  output out_10,
  output out_11
);

  wire nand_1_out, nand_2_out, nand_3_out, nand_4_out, nand_5_out, nand_6_out, nand_7_out, nand_8_out,
       nand_9_out, nand_10_out, nand_11_out, nand_14_out, nand_15_out, nand_16_out, nand_18_out, nor_1_out,
       nor_2_out, nor_3_out, nor_4_out, nor_5_out, nor_6_out, nor_7_out, nor_8_out, nor_9_out, nor_10_out,
       nor_11_out, nor_12_out, not_1_out, not_2_out, not_3_out, not_5_out, not_6_out, not_8_out, not_9_out,
       not_10_out;

  not not_1 (not_1_out, D3);
  not not_2 (not_2_out, D1);
  not not_3 (not_3_out, D0);
  nor nor_1 (nor_1_out, D2, 1'b0);
  nor nor_2 (nor_2_out, D0, D2);
  nand nand_1 (nand_1_out, D0, D2);
  nand nand_2 (nand_2_out, not_1_out, D1);
  nand nand_3 (nand_3_out, D1, nor_1_out);
  nand nand_4 (nand_4_out, not_2_out, D2);
  nand nand_5 (nand_5_out, not_2_out, nor_1_out);
  nand nand_6 (nand_6_out, nor_1_out, not_3_out);
  nand nand_7 (nand_7_out, nor_1_out, not_1_out);
  nor nor_3 (nor_3_out, not_3_out, D3);
  nor nor_4 (nor_4_out, not_2_out, D3);
  nand nand_8 (nand_8_out, nand_5_out, nand_2_out);
  nand nand_9 (nand_9_out, nand_3_out, nand_4_out);
  nand nand_10 (nand_10_out, nand_6_out, not_1_out);
  nand nand_11 (nand_11_out, nand_8_out, not_3_out);
  nor nor_5 (nor_5_out, D3, nand_9_out);
  nand nand_12 (out_11, nand_10_out, nand_5_out);
  not not_4 (out_9, nand_11_out);
  not not_5 (not_5_out, out_11);
  nor nor_6 (nor_6_out, nor_5_out, not_5_out);
  nor nor_7 (nor_7_out, not_5_out, nand_1_out);
  nor nor_8 (nor_8_out, nor_2_out, nor_6_out);
  nand nand_13 (out_8, nor_8_out, nand_11_out);
  nand nand_14 (nand_14_out, D1, out_8);
  nand nand_15 (nand_15_out, nand_7_out, out_8);
  nand nand_16 (nand_16_out, nor_3_out, out_8);
  not not_6 (not_6_out, nand_14_out);
  not not_7 (out_7, nand_15_out);
  nor nor_9 (nor_9_out, D2, nand_15_out);
  nand nand_17 (out_10, nand_11_out, nand_16_out);
  nand nand_18 (nand_18_out, nor_4_out, nand_15_out);
  nor nor_10 (nor_10_out, not_6_out, nor_7_out);
  not not_8 (not_8_out, nor_9_out);
  not not_9 (not_9_out, out_10);
  nand nand_19 (out_6, not_8_out, nor_10_out);
  nor nor_11 (nor_11_out, not_9_out, D3);
  nor nor_12 (nor_12_out, not_5_out, nor_11_out);
  not not_10 (not_10_out, nor_12_out);
  nand nand_20 (out_5, not_10_out, nand_18_out);
endmodule

module demo (
  input  resetdate,
  input  Reset,
  input  [3:0] ho1,
  input  [3:0] ho0,
  input  [3:0] mi1,
  input  [3:0] mi0,
  input  [3:0] se1,
  input  [3:0] se0,
  input  in_9,
  input  in_10,
  input  in_11,
  input  in_12
);

  wire basic_1_out_9, basic_1_out_10, basic_1_out_11, basic_1_out_12, basic_1_out_13, basic_1_out_14,
       basic_1_out_15, basic_1_out_16, basic_1_out_17, basic_1_out_18, basic_1_out_19, basic_1_out_20,
       basic_1_out_21, basic_1_out_22, basic_1_out_23, basic_1_out_24, basic_1_out_25, basic_1_out_26,
       basic_1_out_27, basic_1_out_28, basic_1_out_29, basic_1_out_30, basic_1_out_31, basic_1_out_32,
       basic_1_out_33, button_1_out, button_2_out, button_3_out, button_4_out, button_5_out, button_6_out,
       button_7_out, button_8_out, button_9_out, button_10_out, button_11_out, button_12_out, clock_1_out,
       date_1_out_11, date_1_out_12, date_1_out_13, date_1_out_14, date_1_out_15, date_1_out_16,
       date_1_out_17, date_1_out_18, date_1_out_19, date_1_out_20, date_1_out_21, date_1_out_22,
       date_1_out_23, date_1_out_24, date_1_out_25, date_1_out_26, date_1_out_27, date_1_out_28,
       date_1_out_29, date_1_out_30, date_1_out_31, date_1_out_32, date_1_out_33, date_1_out_34,
       date_1_out_35, date_1_out_36, date_1_out_37, date_1_out_38, date_1_out_39, date_1_out_40,
       date_1_out_41, date_1_out_42, naozhong_1_light, or_1_out, sevenbit_1_out_5, sevenbit_1_out_6,
       sevenbit_1_out_7, sevenbit_1_out_8, sevenbit_1_out_9, sevenbit_1_out_10, sevenbit_1_out_11,
       sevenbit_2_out_5, sevenbit_2_out_6, sevenbit_2_out_7, sevenbit_2_out_8, sevenbit_2_out_9,
       sevenbit_2_out_10, sevenbit_2_out_11, sevenbit_3_out_5, sevenbit_3_out_6, sevenbit_3_out_7,
       sevenbit_3_out_8, sevenbit_3_out_9, sevenbit_3_out_10, sevenbit_3_out_11, sevenbit_4_out_5,
       sevenbit_4_out_6, sevenbit_4_out_7, sevenbit_4_out_8, sevenbit_4_out_9, sevenbit_4_out_10,
       sevenbit_4_out_11, sevenbit_5_out_5, sevenbit_5_out_6, sevenbit_5_out_7, sevenbit_5_out_8,
       sevenbit_5_out_9, sevenbit_5_out_10, sevenbit_5_out_11, sevenbit_6_out_5, sevenbit_6_out_6,
       sevenbit_6_out_7, sevenbit_6_out_8, sevenbit_6_out_9, sevenbit_6_out_10, sevenbit_6_out_11,
       sevenbit_7_out_5, sevenbit_7_out_6, sevenbit_7_out_7, sevenbit_7_out_8, sevenbit_7_out_9,
       sevenbit_7_out_10, sevenbit_7_out_11, sevenbit_8_out_5, sevenbit_8_out_6, sevenbit_8_out_7,
       sevenbit_8_out_8, sevenbit_8_out_9, sevenbit_8_out_10, sevenbit_8_out_11, sevenbit_9_out_5,
       sevenbit_9_out_6, sevenbit_9_out_7, sevenbit_9_out_8, sevenbit_9_out_9, sevenbit_9_out_10,
       sevenbit_9_out_11, sevenbit_10_out_5, sevenbit_10_out_6, sevenbit_10_out_7, sevenbit_10_out_8,
       sevenbit_10_out_9, sevenbit_10_out_10, sevenbit_10_out_11, sevenbit_11_out_5, sevenbit_11_out_6,
       sevenbit_11_out_7, sevenbit_11_out_8, sevenbit_11_out_9, sevenbit_11_out_10, sevenbit_11_out_11,
       sevenbit_12_out_5, sevenbit_12_out_6, sevenbit_12_out_7, sevenbit_12_out_8, sevenbit_12_out_9,
       sevenbit_12_out_10, sevenbit_12_out_11, sevenbit_13_out_5, sevenbit_13_out_6, sevenbit_13_out_7,
       sevenbit_13_out_8, sevenbit_13_out_9, sevenbit_13_out_10, sevenbit_13_out_11, sevenbit_14_out_5,
       sevenbit_14_out_6, sevenbit_14_out_7, sevenbit_14_out_8, sevenbit_14_out_9, sevenbit_14_out_10,
       sevenbit_14_out_11, undriven;

  LED led_1 (.in(naozhong_1_light));
  LED led_2 (.in(naozhong_1_light));
  LED led_3 (.in(naozhong_1_light));
  LED led_4 (.in(naozhong_1_light));
  LED led_5 (.in(naozhong_1_light));
  LED led_6 (.in(naozhong_1_light));
  LED led_7 (.in(naozhong_1_light));
  LED led_8 (.in(naozhong_1_light));
  LED led_9 (.in(naozhong_1_light));
  LED led_10 (.in(naozhong_1_light));
  LED led_11 (.in(naozhong_1_light));
  LED led_12 (.in(naozhong_1_light));
  LED led_13 (.in(naozhong_1_light));
  LED led_14 (.in(naozhong_1_light));
  LED led_15 (.in(naozhong_1_light));
  LED led_16 (.in(naozhong_1_light));
  LED led_17 (.in(naozhong_1_light));
  LED led_18 (.in(naozhong_1_light));
  LED led_19 (.in(naozhong_1_light));
  LED led_20 (.in(naozhong_1_light));
  LED led_21 (.in(naozhong_1_light));
  LED led_22 (.in(naozhong_1_light));
  LED led_23 (.in(naozhong_1_light));
  LED led_24 (.in(naozhong_1_light));
  LED led_25 (.in(naozhong_1_light));
  LED led_26 (.in(naozhong_1_light));
  LED led_27 (.in(naozhong_1_light));
  LED led_28 (.in(naozhong_1_light));
  LED led_29 (.in(naozhong_1_light));
  LED led_30 (.in(naozhong_1_light));
  LED led_31 (.in(naozhong_1_light));
  LED led_32 (.in(naozhong_1_light));
  LED led_33 (.in(naozhong_1_light));
  LED led_34 (.in(naozhong_1_light));
  LED led_35 (.in(naozhong_1_light));
  LED led_36 (.in(naozhong_1_light));
  LED led_37 (.in(naozhong_1_light));
  LED led_38 (.in(naozhong_1_light));
  LED led_39 (.in(naozhong_1_light));
  LED led_40 (.in(naozhong_1_light));
  LED led_41 (.in(naozhong_1_light));
  LED led_42 (.in(naozhong_1_light));
  LED led_43 (.in(naozhong_1_light));
  LED led_44 (.in(naozhong_1_light));
  LED led_45 (.in(naozhong_1_light));
  LED led_46 (.in(naozhong_1_light));
  LED led_47 (.in(naozhong_1_light));
  LED led_48 (.in(naozhong_1_light));
  LED led_49 (.in(naozhong_1_light));
  LED led_50 (.in(naozhong_1_light));
  LED led_51 (.in(naozhong_1_light));
  LED led_52 (.in(naozhong_1_light));
  NaoZhong naozhong_1 (
    .Light(naozhong_1_light), .Reset(Reset), .m0(mi0), .s1(se1), .s0(se0), .h1(ho1), .h0(ho0), .m1(mi1),
    .M0D3(basic_1_out_21), .S0D3(basic_1_out_29), .H0D3(basic_1_out_13), .M0D2(basic_1_out_22),
    .M0D1(basic_1_out_23), .M0D0(basic_1_out_24), .S1D3(basic_1_out_25), .S1D2(basic_1_out_26),
    .S1D1(basic_1_out_27), .S1D0(basic_1_out_28), .S0D2(basic_1_out_30), .S0D1(basic_1_out_31),
    .S0D0(basic_1_out_32), .H1D3(basic_1_out_9), .H1D2(basic_1_out_10), .H1D1(basic_1_out_11),
    .H1D0(basic_1_out_12), .H0D2(basic_1_out_14), .H0D1(basic_1_out_15), .H0D0(basic_1_out_16),
    .M1D3(basic_1_out_17), .M1D2(basic_1_out_18), .M1D1(basic_1_out_19), .M1D0(basic_1_out_20));
  LED led_53 (.in(naozhong_1_light));
  LED led_54 (.in(naozhong_1_light));
  LED led_55 (.in(naozhong_1_light));
  LED led_56 (.in(naozhong_1_light));
  LED led_57 (.in(naozhong_1_light));
  LED led_58 (.in(naozhong_1_light));
  LED led_59 (.in(naozhong_1_light));
  LED led_60 (.in(naozhong_1_light));
  LED led_61 (.in(naozhong_1_light));
  LED led_62 (.in(naozhong_1_light));
  LED led_63 (.in(naozhong_1_light));
  LED led_64 (.in(naozhong_1_light));
  LED led_65 (.in(naozhong_1_light));
  LED led_66 (.in(naozhong_1_light));
  LED led_67 (.in(naozhong_1_light));
  Date date_1 (
    .out_17(date_1_out_17), .out_16(date_1_out_16), .out_32(date_1_out_32), .out_18(date_1_out_18),
    .out_15(date_1_out_15), .out_31(date_1_out_31), .out_19(date_1_out_19), .out_14(date_1_out_14),
    .out_30(date_1_out_30), .out_20(date_1_out_20), .out_13(date_1_out_13), .out_29(date_1_out_29),
    .out_21(date_1_out_21), .out_12(date_1_out_12), .out_28(date_1_out_28), .out_22(date_1_out_22),
    .out_11(date_1_out_11), .out_27(date_1_out_27), .out_23(date_1_out_23), .in_2(basic_1_out_33),
    .out_26(date_1_out_26), .out_24(date_1_out_24), .in_1(resetdate), .out_25(date_1_out_25),
    .out_33(date_1_out_33), .out_34(date_1_out_34), .out_35(date_1_out_35), .out_36(date_1_out_36),
    .out_37(date_1_out_37), .out_38(date_1_out_38), .out_39(date_1_out_39), .out_40(date_1_out_40),
    .out_41(date_1_out_41), .out_42(date_1_out_42), .year3(button_1_out), .year2(button_2_out),
    .year1(button_3_out), .year0(button_4_out), .month1(button_5_out), .month0(button_7_out),
    .day1(button_8_out), .day0(button_10_out));
  _7_Segment_Display u_7_segment_display_1 (
    .g(sevenbit_2_out_8), .f(sevenbit_2_out_7), .a(sevenbit_2_out_6), .b(sevenbit_2_out_5),
    .e(sevenbit_2_out_9), .d(sevenbit_2_out_10), .c(sevenbit_2_out_11));  // open: dp
  sevenbit sevenbit_1 (
    .out_6(sevenbit_1_out_6), .out_5(sevenbit_1_out_5), .out_7(sevenbit_1_out_7), .out_8(sevenbit_1_out_8),
    .out_9(sevenbit_1_out_9), .out_10(sevenbit_1_out_10), .out_11(sevenbit_1_out_11), .D3(basic_1_out_9),
    .D2(basic_1_out_10), .D1(basic_1_out_11), .D0(basic_1_out_12));
  sevenbit sevenbit_2 (
    .out_6(sevenbit_2_out_6), .out_5(sevenbit_2_out_5), .out_7(sevenbit_2_out_7), .out_8(sevenbit_2_out_8),
    .out_9(sevenbit_2_out_9), .out_10(sevenbit_2_out_10), .out_11(sevenbit_2_out_11), .D3(date_1_out_11),
    .D2(date_1_out_12), .D1(date_1_out_13), .D0(date_1_out_14));
  _7_Segment_Display u_7_segment_display_2 (
    .g(sevenbit_1_out_8), .f(sevenbit_1_out_7), .a(sevenbit_1_out_6), .b(sevenbit_1_out_5),
    .e(sevenbit_1_out_9), .d(sevenbit_1_out_10), .c(sevenbit_1_out_11));  // open: dp
  Basic basic_1 (
    .out_18(basic_1_out_18), .out_19(basic_1_out_19), .out_20(basic_1_out_20), .out_21(basic_1_out_21),
    .out_22(basic_1_out_22), .out_23(basic_1_out_23), .out_24(basic_1_out_24), .out_25(basic_1_out_25),
    .out_26(basic_1_out_26), .out_27(basic_1_out_27), .out_28(basic_1_out_28), .out_29(basic_1_out_29),
    .out_30(basic_1_out_30), .out_31(basic_1_out_31), .out_32(basic_1_out_32), .out_9(basic_1_out_9),
    .out_10(basic_1_out_10), .out_11(basic_1_out_11), .out_12(basic_1_out_12), .out_13(basic_1_out_13),
    .out_14(basic_1_out_14), .out_15(basic_1_out_15), .out_16(basic_1_out_16), .out_17(basic_1_out_17),
    .M(button_11_out), .S(button_12_out), .CLK(undriven), .Pause(in_11), .Reset(button_6_out),
    .TwelveHour(in_10), .TwoFourHour(in_9), .H(or_1_out), .out_33(basic_1_out_33));
  LED led_68 (.in(in_9));
  _7_Segment_Display u_7_segment_display_3 (
    .g(sevenbit_4_out_8), .f(sevenbit_4_out_7), .a(sevenbit_4_out_6), .b(sevenbit_4_out_5),
    .e(sevenbit_4_out_9), .d(sevenbit_4_out_10), .c(sevenbit_4_out_11));  // open: dp
  sevenbit sevenbit_3 (
    .out_6(sevenbit_3_out_6), .out_5(sevenbit_3_out_5), .out_7(sevenbit_3_out_7), .out_8(sevenbit_3_out_8),
    .out_9(sevenbit_3_out_9), .out_10(sevenbit_3_out_10), .out_11(sevenbit_3_out_11), .D3(basic_1_out_13),
    .D2(basic_1_out_14), .D1(basic_1_out_15), .D0(basic_1_out_16));
  LED led_69 (.in(in_10));
  sevenbit sevenbit_4 (
    .out_6(sevenbit_4_out_6), .out_5(sevenbit_4_out_5), .out_7(sevenbit_4_out_7), .out_8(sevenbit_4_out_8),
    .out_9(sevenbit_4_out_9), .out_10(sevenbit_4_out_10), .out_11(sevenbit_4_out_11), .D3(date_1_out_15),
    .D2(date_1_out_16), .D1(date_1_out_17), .D0(date_1_out_18));
  _7_Segment_Display u_7_segment_display_4 (
    .g(sevenbit_3_out_8), .f(sevenbit_3_out_7), .a(sevenbit_3_out_6), .b(sevenbit_3_out_5),
    .e(sevenbit_3_out_9), .d(sevenbit_3_out_10), .c(sevenbit_3_out_11));  // open: dp
  _7_Segment_Display u_7_segment_display_5 (
    .g(sevenbit_5_out_8), .f(sevenbit_5_out_7), .a(sevenbit_5_out_6), .b(sevenbit_5_out_5),
    .e(sevenbit_5_out_9), .d(sevenbit_5_out_10), .c(sevenbit_5_out_11));  // open: dp
  sevenbit sevenbit_5 (
    .out_6(sevenbit_5_out_6), .out_5(sevenbit_5_out_5), .out_7(sevenbit_5_out_7), .out_8(sevenbit_5_out_8),
    .out_9(sevenbit_5_out_9), .out_10(sevenbit_5_out_10), .out_11(sevenbit_5_out_11), .D3(date_1_out_19),
    .D2(date_1_out_20), .D1(date_1_out_21), .D0(date_1_out_22));
  sevenbit sevenbit_6 (
    .out_6(sevenbit_6_out_6), .out_5(sevenbit_6_out_5), .out_7(sevenbit_6_out_7), .out_8(sevenbit_6_out_8),
    .out_9(sevenbit_6_out_9), .out_10(sevenbit_6_out_10), .out_11(sevenbit_6_out_11), .D3(basic_1_out_17),
    .D2(basic_1_out_18), .D1(basic_1_out_19), .D0(basic_1_out_20));
  Clock CLK ();  // open: out
  Button button_1 (.out(button_1_out));
  _7_Segment_Display u_7_segment_display_6 (
    .g(sevenbit_7_out_8), .f(sevenbit_7_out_7), .a(sevenbit_7_out_6), .b(sevenbit_7_out_5),
    .e(sevenbit_7_out_9), .d(sevenbit_7_out_10), .c(sevenbit_7_out_11));  // open: dp
  _7_Segment_Display u_7_segment_display_7 (
    .g(sevenbit_6_out_8), .f(sevenbit_6_out_7), .a(sevenbit_6_out_6), .b(sevenbit_6_out_5),
    .e(sevenbit_6_out_9), .d(sevenbit_6_out_10), .c(sevenbit_6_out_11));  // open: dp
  Button button_2 (.out(button_2_out));
  sevenbit sevenbit_7 (
    .out_6(sevenbit_7_out_6), .out_5(sevenbit_7_out_5), .out_7(sevenbit_7_out_7), .out_8(sevenbit_7_out_8),
    .out_9(sevenbit_7_out_9), .out_10(sevenbit_7_out_10), .out_11(sevenbit_7_out_11), .D3(date_1_out_23),
    .D2(date_1_out_24), .D1(date_1_out_25), .D0(date_1_out_26));
  sevenbit sevenbit_8 (
    .out_6(sevenbit_8_out_6), .out_5(sevenbit_8_out_5), .out_7(sevenbit_8_out_7), .out_8(sevenbit_8_out_8),
    .out_9(sevenbit_8_out_9), .out_10(sevenbit_8_out_10), .out_11(sevenbit_8_out_11), .D3(basic_1_out_21),
    .D2(basic_1_out_22), .D1(basic_1_out_23), .D0(basic_1_out_24));
  Button button_3 (.out(button_3_out));
  _7_Segment_Display u_7_segment_display_8 (
    .g(sevenbit_8_out_8), .f(sevenbit_8_out_7), .a(sevenbit_8_out_6), .b(sevenbit_8_out_5),
    .e(sevenbit_8_out_9), .d(sevenbit_8_out_10), .c(sevenbit_8_out_11));  // open: dp
  Button button_4 (.out(button_4_out));
  _7_Segment_Display u_7_segment_display_9 (
    .g(sevenbit_9_out_8), .f(sevenbit_9_out_7), .a(sevenbit_9_out_6), .b(sevenbit_9_out_5),
    .e(sevenbit_9_out_9), .d(sevenbit_9_out_10), .c(sevenbit_9_out_11));  // open: dp
  Button button_5 (.out(button_5_out));
  sevenbit sevenbit_9 (
    .out_6(sevenbit_9_out_6), .out_5(sevenbit_9_out_5), .out_7(sevenbit_9_out_7), .out_8(sevenbit_9_out_8),
    .out_9(sevenbit_9_out_9), .out_10(sevenbit_9_out_10), .out_11(sevenbit_9_out_11), .D3(date_1_out_27),
    .D2(date_1_out_28), .D1(date_1_out_29), .D0(date_1_out_30));
  sevenbit sevenbit_10 (
    .out_6(sevenbit_10_out_6), .out_5(sevenbit_10_out_5), .out_7(sevenbit_10_out_7),
    .out_8(sevenbit_10_out_8), .out_9(sevenbit_10_out_9), .out_10(sevenbit_10_out_10),
    .out_11(sevenbit_10_out_11), .D3(basic_1_out_25), .D2(basic_1_out_26), .D1(basic_1_out_27),
    .D0(basic_1_out_28));
  Button button_6 (.out(button_6_out));
  Button button_7 (.out(button_7_out));
  _7_Segment_Display u_7_segment_display_10 (
    .g(sevenbit_11_out_8), .f(sevenbit_11_out_7), .a(sevenbit_11_out_6), .b(sevenbit_11_out_5),
    .e(sevenbit_11_out_9), .d(sevenbit_11_out_10), .c(sevenbit_11_out_11));  // open: dp
  or or_1 (or_1_out, button_9_out, clock_1_out);
  Clock clock_1 (.out(clock_1_out));
  Button button_8 (.out(button_8_out));
  sevenbit sevenbit_11 (
    .out_6(sevenbit_11_out_6), .out_5(sevenbit_11_out_5), .out_7(sevenbit_11_out_7),
    .out_8(sevenbit_11_out_8), .out_9(sevenbit_11_out_9), .out_10(sevenbit_11_out_10),
    .out_11(sevenbit_11_out_11), .D3(date_1_out_31), .D2(date_1_out_32), .D1(date_1_out_33),
    .D0(date_1_out_34));
  _7_Segment_Display u_7_segment_display_11 (
    .g(sevenbit_10_out_8), .f(sevenbit_10_out_7), .a(sevenbit_10_out_6), .b(sevenbit_10_out_5),
    .e(sevenbit_10_out_9), .d(sevenbit_10_out_10), .c(sevenbit_10_out_11));  // open: dp
  sevenbit sevenbit_12 (
    .out_6(sevenbit_12_out_6), .out_5(sevenbit_12_out_5), .out_7(sevenbit_12_out_7),
    .out_8(sevenbit_12_out_8), .out_9(sevenbit_12_out_9), .out_10(sevenbit_12_out_10),
    .out_11(sevenbit_12_out_11), .D3(basic_1_out_29), .D2(basic_1_out_30), .D1(basic_1_out_31),
    .D0(basic_1_out_32));
  Button button_9 (.out(button_9_out));
  Button button_10 (.out(button_10_out));
  _7_Segment_Display u_7_segment_display_12 (
    .g(sevenbit_13_out_8), .f(sevenbit_13_out_7), .a(sevenbit_13_out_6), .b(sevenbit_13_out_5),
    .e(sevenbit_13_out_9), .d(sevenbit_13_out_10), .c(sevenbit_13_out_11));  // open: dp
  Button button_11 (.out(button_11_out));
  Button button_12 (.out(button_12_out));
  sevenbit sevenbit_13 (
    .out_6(sevenbit_13_out_6), .out_5(sevenbit_13_out_5), .out_7(sevenbit_13_out_7),
    .out_8(sevenbit_13_out_8), .out_9(sevenbit_13_out_9), .out_10(sevenbit_13_out_10),
    .out_11(sevenbit_13_out_11), .D3(date_1_out_35), .D2(date_1_out_36), .D1(date_1_out_37),
    .D0(date_1_out_38));
  _7_Segment_Display u_7_segment_display_13 (
    .g(sevenbit_12_out_8), .f(sevenbit_12_out_7), .a(sevenbit_12_out_6), .b(sevenbit_12_out_5),
    .e(sevenbit_12_out_9), .d(sevenbit_12_out_10), .c(sevenbit_12_out_11));  // open: dp
  _7_Segment_Display u_7_segment_display_14 (
    .g(sevenbit_14_out_8), .f(sevenbit_14_out_7), .a(sevenbit_14_out_6), .b(sevenbit_14_out_5),
    .e(sevenbit_14_out_9), .d(sevenbit_14_out_10), .c(sevenbit_14_out_11));  // open: dp
  sevenbit sevenbit_14 (
    .out_6(sevenbit_14_out_6), .out_5(sevenbit_14_out_5), .out_7(sevenbit_14_out_7),
    .out_8(sevenbit_14_out_8), .out_9(sevenbit_14_out_9), .out_10(sevenbit_14_out_10),
    .out_11(sevenbit_14_out_11), .D3(date_1_out_39), .D2(date_1_out_40), .D1(date_1_out_41),
    .D0(date_1_out_42));

  // Notes on the sheet:
  //   Reset为1时复位（或者说是关闭）
  //   24H
  //   使用时调至高电平即可
  //   Hour
  //   12H
  //   暂停：调至高电平即可停止运行
  //   Minute
  //   初始化
  //   Second
  //   H
  //   设置初始时间
  //   M
  //   S
  //   倒计时功能，升至高电平时闹钟倒着走
  //   功能尚未完成
endmodule

module fourbitcounter (
  input  T,
  input  Pause,
  input  Reset,
  output out_4,
  output out_5,
  output out_6,
  output out_7
);

  wire and_1_out, not_1_out, t_ff_1_qn, t_ff_2_qn, t_ff_3_qn;

  not not_1 (not_1_out, Pause);
  T_Flip_Flop t_ff_1 (.T(1'b1), .clk(and_1_out), .Q(out_7), .Qn(t_ff_1_qn), .reset(Reset));  // open: preset
  and and_1 (and_1_out, T, not_1_out);
  T_Flip_Flop t_ff_2 (.T(1'b1), .clk(t_ff_1_qn), .Q(out_6), .Qn(t_ff_2_qn), .reset(Reset));  // open: preset
  T_Flip_Flop t_ff_3 (.T(1'b1), .clk(t_ff_2_qn), .Q(out_5), .Qn(t_ff_3_qn), .reset(Reset));  // open: preset
  T_Flip_Flop t_ff_4 (.T(1'b1), .clk(t_ff_3_qn), .Q(out_4), .reset(Reset));  // open: Qn, preset
endmodule

module Basic (
  input  TwelveHour,
  input  TwoFourHour,
  input  CLK,
  input  Pause,
  input  Reset,
  input  H,
  input  M,
  input  S,
  output out_9,
  output out_10,
  output out_11,
  output out_12,
  output out_13,
  output out_14,
  output out_15,
  output out_16,
  output out_17,
  output out_18,
  output out_19,
  output out_20,
  output out_21,
  output out_22,
  output out_23,
  output out_24,
  output out_25,
  output out_26,
  output out_27,
  output out_28,
  output out_29,
  output out_30,
  output out_31,
  output out_32,
  output out_33
);

  wire and_1_out, and_3_out, and_4_out, and_5_out, and_6_out, and_7_out, or_1_out, or_2_out, or_3_out,
       or_4_out, or_5_out, or_6_out, or_7_out, or_8_out, or_9_out;

  and and_1 (and_1_out, out_15, TwelveHour, out_12);
  and and_2 (out_33, out_14, TwoFourHour, out_11);
  fourbitcounter fourbitcounter_1 (
    .out_4(out_9), .out_5(out_10), .out_6(out_11), .out_7(out_12), .Pause(Pause), .T(and_3_out),
    .Reset(or_1_out));
  or or_1 (or_1_out, out_33, and_1_out, Reset);
  and and_3 (and_3_out, out_13, out_15);
  fourbitcounter fourbitcounter_2 (
    .out_4(out_13), .out_5(out_14), .out_6(out_15), .out_7(out_16), .Pause(Pause), .T(or_3_out),
    .Reset(or_2_out));
  or or_2 (or_2_out, and_3_out, out_33, and_1_out, Reset);
  or or_3 (or_3_out, and_4_out, H);
  and and_4 (and_4_out, out_18, out_19);
  fourbitcounter fourbitcounter_3 (
    .out_4(out_17), .out_5(out_18), .out_6(out_19), .out_7(out_20), .Pause(Pause), .T(and_5_out),
    .Reset(or_4_out));
  or or_4 (or_4_out, and_4_out, Reset);
  and and_5 (and_5_out, out_21, out_23);
  fourbitcounter fourbitcounter_4 (
    .out_4(out_21), .out_5(out_22), .out_6(out_23), .out_7(out_24), .Pause(Pause), .T(or_6_out),
    .Reset(or_5_out));
  or or_5 (or_5_out, and_5_out, Reset);
  or or_6 (or_6_out, and_6_out, M);
  and and_6 (and_6_out, out_26, out_27);
  fourbitcounter fourbitcounter_5 (
    .out_4(out_25), .out_5(out_26), .out_6(out_27), .out_7(out_28), .Pause(Pause), .T(and_7_out),
    .Reset(or_7_out));
  or or_7 (or_7_out, and_6_out, Reset);
  and and_7 (and_7_out, out_29, out_31);
  fourbitcounter fourbitcounter_6 (
    .out_4(out_29), .out_5(out_30), .out_6(out_31), .out_7(out_32), .Pause(Pause), .T(or_9_out),
    .Reset(or_8_out));
  or or_8 (or_8_out, and_7_out, Reset);
  or or_9 (or_9_out, CLK, S);

  // Notes on the sheet:
  //   调节时间（支持上调）
endmodule

module NaoZhong (
  input  H1D3,
  input  H1D2,
  input  H1D1,
  input  [3:0] h1,
  input  H1D0,
  input  H0D3,
  input  H0D2,
  input  H0D1,
  input  [3:0] h0,
  input  H0D0,
  input  M1D3,
  input  M1D2,
  input  M1D1,
  input  [3:0] m1,
  input  M1D0,
  input  M0D3,
  input  M0D2,
  input  Reset,
  input  M0D1,
  input  [3:0] m0,
  input  M0D0,
  input  S1D3,
  input  S1D2,
  input  S1D1,
  input  [3:0] s1,
  input  S1D0,
  input  S0D3,
  input  S0D2,
  input  S0D1,
  input  [3:0] s0,
  input  S0D0,
  output Light
);

  wire and_1_out, and_2_out, and_3_out, and_4_out, and_5_out, and_6_out, and_7_out, and_8_out, and_9_out,
       and_10_out, xnor_1_out, xnor_2_out, xnor_3_out, xnor_4_out, xnor_5_out, xnor_6_out, xnor_7_out,
       xnor_8_out, xnor_9_out, xnor_10_out, xnor_11_out, xnor_12_out, xnor_13_out, xnor_14_out, xnor_15_out,
       xnor_16_out, xnor_17_out, xnor_18_out, xnor_19_out, xnor_20_out, xnor_21_out, xnor_22_out,
       xnor_23_out, xnor_24_out;

  xnor xnor_1 (xnor_1_out, H1D3, h1[3]);
  xnor xnor_2 (xnor_2_out, H1D2, h1[2]);
  xnor xnor_3 (xnor_3_out, H1D1, h1[1]);
  xnor xnor_4 (xnor_4_out, H1D0, h1[0]);
  xnor xnor_5 (xnor_5_out, H0D3, h0[3]);
  xnor xnor_6 (xnor_6_out, H0D2, h0[2]);
  xnor xnor_7 (xnor_7_out, H0D1, h0[1]);
  xnor xnor_8 (xnor_8_out, H0D0, h0[0]);
  xnor xnor_9 (xnor_9_out, M1D3, m1[3]);
  xnor xnor_10 (xnor_10_out, M1D2, m1[2]);
  xnor xnor_11 (xnor_11_out, M1D1, m1[1]);
  xnor xnor_12 (xnor_12_out, M1D0, m1[0]);
  xnor xnor_13 (xnor_13_out, M0D3, m0[3]);
  xnor xnor_14 (xnor_14_out, M0D2, m0[2]);
  xnor xnor_15 (xnor_15_out, M0D1, m0[1]);
  xnor xnor_16 (xnor_16_out, M0D0, m0[0]);
  xnor xnor_17 (xnor_17_out, S1D3, s1[3]);
  xnor xnor_18 (xnor_18_out, S1D2, s1[2]);
  xnor xnor_19 (xnor_19_out, S1D1, s1[1]);
  xnor xnor_20 (xnor_20_out, S1D0, s1[0]);
  xnor xnor_21 (xnor_21_out, S0D3, s0[3]);
  xnor xnor_22 (xnor_22_out, S0D2, s0[2]);
  xnor xnor_23 (xnor_23_out, S0D1, s0[1]);
  xnor xnor_24 (xnor_24_out, S0D0, s0[0]);
  and and_1 (and_1_out, xnor_1_out, xnor_2_out, xnor_3_out, xnor_4_out);
  and and_2 (and_2_out, xnor_5_out, xnor_6_out, xnor_7_out, xnor_8_out);
  and and_3 (and_3_out, xnor_9_out, xnor_10_out, xnor_11_out, xnor_12_out);
  and and_4 (and_4_out, xnor_13_out, xnor_14_out, xnor_15_out, xnor_16_out);
  and and_5 (and_5_out, xnor_17_out, xnor_18_out, xnor_19_out, xnor_20_out);
  and and_6 (and_6_out, xnor_21_out, xnor_22_out, xnor_23_out, xnor_24_out);
  and and_7 (and_7_out, and_1_out, and_2_out);
  and and_8 (and_8_out, and_3_out, and_4_out);
  and and_9 (and_9_out, and_5_out, and_6_out);
  and and_10 (and_10_out, and_7_out, and_8_out, and_9_out);
  D_Flip_Flop d_ff_1 (.D(1'b1), .clk(and_10_out), .Q(Light), .reset(Reset));  // open: Qn, preset
endmodule

module BasicReverse (
  input  Reset,
  output out_2
);

  wire and_2_out, and_3_out, and_4_out, and_5_out, and_6_out, and_7_out, and_8_out, and_9_out, button_1_out,
       button_2_out, button_3_out, button_4_out, button_5_out, button_6_out, clock_1_out, d_ff_1_q, d_ff_2_q,
       d_ff_3_q, d_ff_4_q, d_ff_5_q, d_ff_6_q, jianfaqi_1_out_3, jianfaqi_1_out_4, jianfaqi_1_out_5,
       jianfaqi_1_out_6, jianfaqi_2_out_3, jianfaqi_2_out_4, jianfaqi_2_out_5, jianfaqi_2_out_6,
       jianfaqi_3_out_3, jianfaqi_3_out_4, jianfaqi_3_out_5, jianfaqi_3_out_6, jianfaqisix_1_out_3,
       jianfaqisix_1_out_4, jianfaqisix_1_out_5, jianfaqisix_1_out_6, jianfaqisix_2_out_3,
       jianfaqisix_2_out_4, jianfaqisix_2_out_5, jianfaqisix_2_out_6, jianfaqisix_3_out_3,
       jianfaqisix_3_out_4, jianfaqisix_3_out_5, jianfaqisix_3_out_6, not_1_out, not_2_out, not_3_out,
       not_4_out, not_5_out, not_6_out, not_7_out, not_8_out, not_9_out, not_10_out, not_11_out, not_12_out,
       not_13_out, not_14_out, not_15_out, not_16_out, not_17_out, not_18_out, not_19_out, not_20_out,
       not_21_out, not_22_out, not_23_out, not_24_out, or_1_out, or_2_out, or_3_out, or_4_out, or_5_out,
       or_6_out, sevenbit_1_out_5, sevenbit_1_out_6, sevenbit_1_out_7, sevenbit_1_out_8, sevenbit_1_out_9,
       sevenbit_1_out_10, sevenbit_1_out_11, sevenbit_2_out_5, sevenbit_2_out_6, sevenbit_2_out_7,
       sevenbit_2_out_8, sevenbit_2_out_9, sevenbit_2_out_10, sevenbit_2_out_11, sevenbit_3_out_5,
       sevenbit_3_out_6, sevenbit_3_out_7, sevenbit_3_out_8, sevenbit_3_out_9, sevenbit_3_out_10,
       sevenbit_3_out_11, sevenbit_4_out_5, sevenbit_4_out_6, sevenbit_4_out_7, sevenbit_4_out_8,
       sevenbit_4_out_9, sevenbit_4_out_10, sevenbit_4_out_11, sevenbit_5_out_5, sevenbit_5_out_6,
       sevenbit_5_out_7, sevenbit_5_out_8, sevenbit_5_out_9, sevenbit_5_out_10, sevenbit_5_out_11,
       sevenbit_6_out_5, sevenbit_6_out_6, sevenbit_6_out_7, sevenbit_6_out_8, sevenbit_6_out_9,
       sevenbit_6_out_10, sevenbit_6_out_11;

  not not_1 (not_1_out, jianfaqisix_1_out_3);
  not not_2 (not_2_out, jianfaqisix_1_out_4);
  and and_1 (out_2, d_ff_1_q, or_1_out);
  sevenbit sevenbit_1 (
    .out_6(sevenbit_1_out_6), .out_5(sevenbit_1_out_5), .out_7(sevenbit_1_out_7), .out_8(sevenbit_1_out_8),
    .out_9(sevenbit_1_out_9), .out_10(sevenbit_1_out_10), .out_11(sevenbit_1_out_11),
    .D3(jianfaqisix_1_out_3), .D2(jianfaqisix_1_out_4), .D1(jianfaqisix_1_out_5), .D0(jianfaqisix_1_out_6));
  not not_3 (not_3_out, jianfaqisix_1_out_5);
  not not_4 (not_4_out, jianfaqisix_1_out_6);
  Jianfaqisix jianfaqisix_1 (
    .in_1(or_1_out), .in_2(Reset), .out_3(jianfaqisix_1_out_3), .out_4(jianfaqisix_1_out_4),
    .out_5(jianfaqisix_1_out_5), .out_6(jianfaqisix_1_out_6));
  and and_2 (and_2_out, not_1_out, not_2_out, not_3_out, not_4_out);
  D_Flip_Flop d_ff_1 (.D(and_2_out), .clk(and_3_out), .Q(d_ff_1_q), .reset(Reset));  // open: Qn, preset
  or or_1 (or_1_out, d_ff_2_q, button_1_out);
  _7_Segment_Display u_7_segment_display_1 (
    .g(sevenbit_1_out_8), .f(sevenbit_1_out_7), .a(sevenbit_1_out_6), .b(sevenbit_1_out_5),
    .e(sevenbit_1_out_9), .d(sevenbit_1_out_10), .c(sevenbit_1_out_11));  // open: dp
  sevenbit sevenbit_2 (
    .out_6(sevenbit_2_out_6), .out_5(sevenbit_2_out_5), .out_7(sevenbit_2_out_7), .out_8(sevenbit_2_out_8),
    .out_9(sevenbit_2_out_9), .out_10(sevenbit_2_out_10), .out_11(sevenbit_2_out_11), .D3(jianfaqi_1_out_3),
    .D2(jianfaqi_1_out_4), .D1(jianfaqi_1_out_5), .D0(jianfaqi_1_out_6));
  not not_5 (not_5_out, jianfaqi_1_out_6);
  not not_6 (not_6_out, jianfaqi_1_out_3);
  not not_7 (not_7_out, jianfaqi_1_out_5);
  not not_8 (not_8_out, jianfaqi_1_out_4);
  Jianfaqi jianfaqi_1 (
    .in_1(or_2_out), .Reset(Reset), .out_3(jianfaqi_1_out_3), .out_4(jianfaqi_1_out_4),
    .out_5(jianfaqi_1_out_5), .out_6(jianfaqi_1_out_6));
  and and_3 (and_3_out, not_6_out, not_8_out, not_7_out, not_5_out);
  D_Flip_Flop d_ff_2 (.D(and_3_out), .clk(or_2_out), .Q(d_ff_2_q), .reset(Reset));  // open: Qn, preset
  Button button_1 (.out(button_1_out));
  or or_2 (or_2_out, and_5_out, button_2_out);
  Button button_2 (.out(button_2_out));
  _7_Segment_Display u_7_segment_display_2 (
    .g(sevenbit_2_out_8), .f(sevenbit_2_out_7), .a(sevenbit_2_out_6), .b(sevenbit_2_out_5),
    .e(sevenbit_2_out_9), .d(sevenbit_2_out_10), .c(sevenbit_2_out_11));  // open: dp
  not not_9 (not_9_out, jianfaqisix_2_out_4);
  not not_10 (not_10_out, jianfaqisix_2_out_3);
  not not_11 (not_11_out, jianfaqisix_2_out_5);
  and and_4 (and_4_out, not_10_out, not_9_out, not_11_out, not_12_out);
  and and_5 (and_5_out, d_ff_3_q, or_3_out);
  sevenbit sevenbit_3 (
    .out_6(sevenbit_3_out_6), .out_5(sevenbit_3_out_5), .out_7(sevenbit_3_out_7), .out_8(sevenbit_3_out_8),
    .out_9(sevenbit_3_out_9), .out_10(sevenbit_3_out_10), .out_11(sevenbit_3_out_11),
    .D3(jianfaqisix_2_out_3), .D2(jianfaqisix_2_out_4), .D1(jianfaqisix_2_out_5), .D0(jianfaqisix_2_out_6));
  not not_12 (not_12_out, jianfaqisix_2_out_6);
  Jianfaqisix jianfaqisix_2 (
    .in_1(or_3_out), .in_2(Reset), .out_3(jianfaqisix_2_out_3), .out_4(jianfaqisix_2_out_4),
    .out_5(jianfaqisix_2_out_5), .out_6(jianfaqisix_2_out_6));
  D_Flip_Flop d_ff_3 (.D(and_4_out), .clk(and_6_out), .Q(d_ff_3_q), .reset(Reset));  // open: Qn, preset
  or or_3 (or_3_out, d_ff_4_q, button_3_out);
  _7_Segment_Display u_7_segment_display_3 (
    .g(sevenbit_3_out_8), .f(sevenbit_3_out_7), .a(sevenbit_3_out_6), .b(sevenbit_3_out_5),
    .e(sevenbit_3_out_9), .d(sevenbit_3_out_10), .c(sevenbit_3_out_11));  // open: dp
  not not_13 (not_13_out, jianfaqi_2_out_4);
  not not_14 (not_14_out, jianfaqi_2_out_3);
  and and_6 (and_6_out, not_14_out, not_13_out, not_15_out, not_16_out);
  Button button_3 (.out(button_3_out));
  sevenbit sevenbit_4 (
    .out_6(sevenbit_4_out_6), .out_5(sevenbit_4_out_5), .out_7(sevenbit_4_out_7), .out_8(sevenbit_4_out_8),
    .out_9(sevenbit_4_out_9), .out_10(sevenbit_4_out_10), .out_11(sevenbit_4_out_11), .D3(jianfaqi_2_out_3),
    .D2(jianfaqi_2_out_4), .D1(jianfaqi_2_out_5), .D0(jianfaqi_2_out_6));
  not not_15 (not_15_out, jianfaqi_2_out_5);
  not not_16 (not_16_out, jianfaqi_2_out_6);
  Jianfaqi jianfaqi_2 (
    .in_1(or_4_out), .Reset(Reset), .out_3(jianfaqi_2_out_3), .out_4(jianfaqi_2_out_4),
    .out_5(jianfaqi_2_out_5), .out_6(jianfaqi_2_out_6));
  D_Flip_Flop d_ff_4 (.D(and_6_out), .clk(or_4_out), .Q(d_ff_4_q), .reset(Reset));  // open: Qn, preset
  _7_Segment_Display u_7_segment_display_4 (
    .g(sevenbit_4_out_8), .f(sevenbit_4_out_7), .a(sevenbit_4_out_6), .b(sevenbit_4_out_5),
    .e(sevenbit_4_out_9), .d(sevenbit_4_out_10), .c(sevenbit_4_out_11));  // open: dp
  or or_4 (or_4_out, and_7_out, button_4_out);
  Button button_4 (.out(button_4_out));
  not not_17 (not_17_out, jianfaqisix_3_out_3);
  not not_18 (not_18_out, jianfaqisix_3_out_4);
  and and_7 (and_7_out, d_ff_5_q, or_5_out);
  sevenbit sevenbit_5 (
    .out_6(sevenbit_5_out_6), .out_5(sevenbit_5_out_5), .out_7(sevenbit_5_out_7), .out_8(sevenbit_5_out_8),
    .out_9(sevenbit_5_out_9), .out_10(sevenbit_5_out_10), .out_11(sevenbit_5_out_11),
    .D3(jianfaqisix_3_out_3), .D2(jianfaqisix_3_out_4), .D1(jianfaqisix_3_out_5), .D0(jianfaqisix_3_out_6));
  not not_19 (not_19_out, jianfaqisix_3_out_6);
  not not_20 (not_20_out, jianfaqisix_3_out_5);
  Jianfaqisix jianfaqisix_3 (
    .in_1(or_5_out), .in_2(Reset), .out_3(jianfaqisix_3_out_3), .out_4(jianfaqisix_3_out_4),
    .out_5(jianfaqisix_3_out_5), .out_6(jianfaqisix_3_out_6));
  and and_8 (and_8_out, not_17_out, not_18_out, not_20_out, not_19_out);
  D_Flip_Flop d_ff_5 (.D(and_8_out), .clk(and_9_out), .Q(d_ff_5_q), .reset(Reset));  // open: Qn, preset
  _7_Segment_Display u_7_segment_display_5 (
    .g(sevenbit_5_out_8), .f(sevenbit_5_out_7), .a(sevenbit_5_out_6), .b(sevenbit_5_out_5),
    .e(sevenbit_5_out_9), .d(sevenbit_5_out_10), .c(sevenbit_5_out_11));  // open: dp
  not not_21 (not_21_out, jianfaqi_3_out_4);
  not not_22 (not_22_out, jianfaqi_3_out_3);
  or or_5 (or_5_out, d_ff_6_q, button_5_out);
  Button button_5 (.out(button_5_out));
  sevenbit sevenbit_6 (
    .out_6(sevenbit_6_out_6), .out_5(sevenbit_6_out_5), .out_7(sevenbit_6_out_7), .out_8(sevenbit_6_out_8),
    .out_9(sevenbit_6_out_9), .out_10(sevenbit_6_out_10), .out_11(sevenbit_6_out_11), .D3(jianfaqi_3_out_3),
    .D2(jianfaqi_3_out_4), .D1(jianfaqi_3_out_5), .D0(jianfaqi_3_out_6));
  not not_23 (not_23_out, jianfaqi_3_out_6);
  not not_24 (not_24_out, jianfaqi_3_out_5);
  Jianfaqi jianfaqi_3 (
    .in_1(or_6_out), .Reset(Reset), .out_3(jianfaqi_3_out_3), .out_4(jianfaqi_3_out_4),
    .out_5(jianfaqi_3_out_5), .out_6(jianfaqi_3_out_6));
  and and_9 (and_9_out, not_22_out, not_21_out, not_24_out, not_23_out);
  D_Flip_Flop d_ff_6 (.D(and_9_out), .clk(or_6_out), .Q(d_ff_6_q), .reset(Reset));  // open: Qn, preset
  or or_6 (or_6_out, button_6_out, clock_1_out);
  Button button_6 (.out(button_6_out));
  _7_Segment_Display u_7_segment_display_6 (
    .g(sevenbit_6_out_8), .f(sevenbit_6_out_7), .a(sevenbit_6_out_6), .b(sevenbit_6_out_5),
    .e(sevenbit_6_out_9), .d(sevenbit_6_out_10), .c(sevenbit_6_out_11));  // open: dp
  Clock clock_1 (.out(clock_1_out));
endmodule

module Jianfaqi (
  input  in_1,
  input  Reset,
  output out_3,
  output out_4,
  output out_5,
  output out_6
);

  wire and_1_out, not_1_out, not_2_out, not_3_out, not_4_out, or_1_out, undriven;
  wire [3:0] d_ff_4_q;

  Subtractor #(.width(4)) subtractor_1 (
    .a(d_ff_4_q), .b(4'b0001), .out({out_3, out_4, out_5, out_6}));  // open: bin, bout
  D_Flip_Flop d_ff_1 (.D(out_3), .clk(in_1), .Q(d_ff_4_q[3]), .preset(or_1_out));  // open: Qn, reset
  D_Flip_Flop d_ff_2 (.D(out_4), .clk(in_1), .Q(d_ff_4_q[2]));  // open: Qn, preset, reset
  D_Flip_Flop d_ff_3 (.D(out_5), .clk(in_1), .Q(d_ff_4_q[1]), .preset(or_1_out), .reset(undriven));  // open: Qn
  D_Flip_Flop d_ff_4 (.D(out_6), .clk(in_1), .Q(d_ff_4_q[0]));  // open: Qn, preset, reset
  or or_1 (or_1_out, and_1_out, Reset);
  not not_1 (not_1_out, d_ff_4_q[3]);
  not not_2 (not_2_out, d_ff_4_q[2]);
  and and_1 (and_1_out, not_1_out, not_2_out, not_3_out, not_4_out);
  not not_3 (not_3_out, d_ff_4_q[1]);
  not not_4 (not_4_out, d_ff_4_q[0]);
endmodule

module Jianfaqisix (
  input  in_1,
  input  in_2,
  output out_3,
  output out_4,
  output out_5,
  output out_6
);

  wire and_1_out, not_1_out, not_2_out, not_3_out, not_4_out, or_1_out, undriven;
  wire [3:0] d_ff_4_q;

  Subtractor #(.width(4)) subtractor_1 (
    .a(d_ff_4_q), .b(4'b0001), .out({out_3, out_4, out_5, out_6}));  // open: bin, bout
  D_Flip_Flop d_ff_1 (.D(out_3), .clk(in_1), .Q(d_ff_4_q[3]));  // open: Qn, preset, reset
  D_Flip_Flop d_ff_2 (.D(out_4), .clk(in_1), .Q(d_ff_4_q[2]), .preset(or_1_out));  // open: Qn, reset
  D_Flip_Flop d_ff_3 (.D(out_5), .clk(in_1), .Q(d_ff_4_q[1]), .preset(or_1_out), .reset(undriven));  // open: Qn
  D_Flip_Flop d_ff_4 (.D(out_6), .clk(in_1), .Q(d_ff_4_q[0]));  // open: Qn, preset, reset
  or or_1 (or_1_out, and_1_out, in_2);
  not not_1 (not_1_out, d_ff_4_q[3]);
  not not_2 (not_2_out, d_ff_4_q[2]);
  and and_1 (and_1_out, not_1_out, not_2_out, not_3_out, not_4_out);
  not not_3 (not_3_out, d_ff_4_q[1]);
  not not_4 (not_4_out, d_ff_4_q[0]);
endmodule

module Jianfaqitwo (
  input  in_1,
  input  in_2,
  output out_3,
  output out_4,
  output out_5,
  output out_6
);

  wire and_1_out, not_1_out, not_2_out, not_3_out, not_4_out;
  wire [3:0] d_ff_4_q;

  Subtractor #(.width(4)) subtractor_1 (
    .a(d_ff_4_q), .b(4'b0001), .out({out_3, out_4, out_5, out_6}));  // open: bin, bout
  D_Flip_Flop d_ff_1 (.D(out_3), .clk(in_1), .Q(d_ff_4_q[3]));  // open: Qn, preset, reset
  D_Flip_Flop d_ff_2 (.D(out_4), .clk(in_1), .Q(d_ff_4_q[2]));  // open: Qn, preset, reset
  D_Flip_Flop d_ff_3 (.D(out_5), .clk(in_1), .Q(d_ff_4_q[1]), .preset(and_1_out));  // open: Qn, reset
  D_Flip_Flop d_ff_4 (.D(out_6), .clk(in_1), .Q(d_ff_4_q[0]), .preset(and_1_out));  // open: Qn, reset
  // OR_Gate or_1 has open pins: in0=and_1_out, in1=in_2, out=open
  not not_1 (not_1_out, d_ff_4_q[3]);
  not not_2 (not_2_out, d_ff_4_q[2]);
  and and_1 (and_1_out, not_1_out, not_2_out, not_3_out, not_4_out);
  not not_3 (not_3_out, d_ff_4_q[1]);
  not not_4 (not_4_out, d_ff_4_q[0]);
endmodule

module Date (
  input  in_1,
  input  in_2,
  input  day0,
  input  day1,
  input  year0,
  input  month1,
  input  month0,
  input  year3,
  input  year2,
  input  year1,
  output out_11,
  output out_12,
  output out_13,
  output out_14,
  output out_15,
  output out_16,
  output out_17,
  output out_18,
  output out_19,
  output out_20,
  output out_21,
  output out_22,
  output out_23,
  output out_24,
  output out_25,
  output out_26,
  output out_27,
  output out_28,
  output out_29,
  output out_30,
  output out_31,
  output out_32,
  output out_33,
  output out_34,
  output out_35,
  output out_36,
  output out_37,
  output out_38,
  output out_39,
  output out_40,
  output out_41,
  output out_42
);

  wire and_1_out, and_2_out, and_3_out, and_4_out, and_5_out, and_6_out, and_7_out, and_8_out, and_9_out,
       and_10_out, or_1_out, or_2_out, or_3_out, or_4_out, or_5_out, or_6_out, or_7_out, or_8_out, or_9_out,
       or_10_out, or_11_out, or_12_out, or_13_out, or_14_out, or_15_out;

  fourbitcounterdate1 fourbitcounterdate1_1 (
    .in_1(or_1_out), .in_3(in_1), .out_4(out_11), .out_5(out_12), .out_6(out_13), .out_7(out_14));  // open: in_2
  or or_1 (or_1_out, year3, and_1_out);
  and and_1 (and_1_out, out_15, out_17);
  fourbitcounterdate1 fourbitcounterdate1_2 (
    .in_1(or_2_out), .in_3(or_3_out), .out_4(out_15), .out_5(out_16), .out_6(out_17), .out_7(out_18));  // open: in_2
  or or_2 (or_2_out, year2, and_2_out);
  or or_3 (or_3_out, and_1_out, in_1);
  and and_2 (and_2_out, out_19, out_21);
  fourbitcounterdate1 fourbitcounterdate1_3 (
    .in_1(or_4_out), .in_3(or_5_out), .out_4(out_19), .out_5(out_20), .out_6(out_21), .out_7(out_22));  // open: in_2
  or or_4 (or_4_out, year1, and_3_out);
  or or_5 (or_5_out, and_2_out, in_1);
  and and_3 (and_3_out, out_23, out_25);
  fourbitcounterdate1 fourbitcounterdate1_4 (
    .in_1(or_6_out), .in_3(or_7_out), .out_4(out_23), .out_5(out_24), .out_6(out_25), .out_7(out_26));  // open: in_2
  or or_6 (or_6_out, year0, and_4_out);
  or or_7 (or_7_out, and_3_out, in_1);
  and and_4 (and_4_out, out_33, out_34, out_30);
  or or_8 (or_8_out, and_4_out, in_1);
  fourbitcounterdate1 fourbitcounterdate1_5 (
    .in_1(or_9_out), .in_3(or_8_out), .out_4(out_27), .out_5(out_28), .out_6(out_29), .out_7(out_30));  // open: in_2
  or or_9 (or_9_out, month1, and_5_out);
  and and_5 (and_5_out, out_31, out_33);
  fourbitcounterdate fourbitcounterdate_1 (
    .in_1(or_11_out), .isZero(and_6_out), .in_4(or_10_out), .out_5(out_31), .out_6(out_32), .out_7(out_33),
    .out_8(out_34));  // open: in_2
  or or_10 (or_10_out, and_5_out, or_8_out, in_1);
  or or_11 (or_11_out, month0, and_7_out);
  and and_6 (and_6_out, out_33, out_30);
  and and_7 (and_7_out, out_37, out_38);
  fourbitcounterdate1 fourbitcounterdate1_6 (
    .in_1(or_12_out), .in_3(or_13_out), .out_4(out_35), .out_5(out_36), .out_6(out_37), .out_7(out_38));  // open: in_2
  or or_12 (or_12_out, day1, and_8_out);
  or or_13 (or_13_out, and_7_out, in_1);
  and and_8 (and_8_out, out_39, out_41);
  fourbitcounterdate fourbitcounterdate_2 (
    .in_1(or_15_out), .isZero(and_10_out), .in_4(or_14_out), .out_5(out_39), .out_6(out_40), .out_7(out_41),
    .out_8(out_42));  // open: in_2
  or or_14 (or_14_out, and_8_out, in_1);
  or or_15 (or_15_out, day0, in_2);
  and and_9 (and_9_out, out_39, out_42);
  and and_10 (and_10_out, and_9_out, out_37);
endmodule

module fourbitcounterdate (
  input  in_1,
  input  in_2,
  input  isZero,
  input  in_4,
  output out_5,
  output out_6,
  output out_7,
  output out_8
);

  wire and_1_out, d_ff_1_q, demultiplexer_1_out0, demultiplexer_1_out1, not_1_out, t_ff_1_qn, t_ff_2_qn,
       t_ff_3_qn;

  not not_1 (not_1_out, in_2);
  D_Flip_Flop d_ff_1 (.D(isZero), .clk(in_1), .Q(d_ff_1_q));  // open: Qn, preset, reset
  T_Flip_Flop t_ff_1 (
    .T(1'b1), .clk(and_1_out), .Q(out_8), .Qn(t_ff_1_qn), .reset(demultiplexer_1_out0),
    .preset(demultiplexer_1_out1));
  and and_1 (and_1_out, in_1, not_1_out);
  Demultiplexer #(.enable("false")) demultiplexer_1 (
    .out0(demultiplexer_1_out0), .out1(demultiplexer_1_out1), .in(in_4), .sel(d_ff_1_q));
  T_Flip_Flop t_ff_2 (.T(1'b1), .clk(t_ff_1_qn), .Q(out_7), .Qn(t_ff_2_qn), .reset(in_4));  // open: preset
  T_Flip_Flop t_ff_3 (.T(1'b1), .clk(t_ff_2_qn), .Q(out_6), .Qn(t_ff_3_qn), .reset(in_4));  // open: preset
  T_Flip_Flop t_ff_4 (.T(1'b1), .clk(t_ff_3_qn), .Q(out_5), .reset(in_4));  // open: Qn, preset
endmodule

module fourbitcounterdate1 (
  input  in_1,
  input  in_2,
  input  in_3,
  output out_4,
  output out_5,
  output out_6,
  output out_7
);

  wire and_1_out, not_1_out, t_ff_1_qn, t_ff_2_qn, t_ff_3_qn;

  not not_1 (not_1_out, in_2);
  T_Flip_Flop t_ff_1 (.T(1'b1), .clk(and_1_out), .Q(out_7), .Qn(t_ff_1_qn), .reset(in_3));  // open: preset
  and and_1 (and_1_out, in_1, not_1_out);
  T_Flip_Flop t_ff_2 (.T(1'b1), .clk(t_ff_1_qn), .Q(out_6), .Qn(t_ff_2_qn), .reset(in_3));  // open: preset
  T_Flip_Flop t_ff_3 (.T(1'b1), .clk(t_ff_2_qn), .Q(out_5), .Qn(t_ff_3_qn), .reset(in_3));  // open: preset
  T_Flip_Flop t_ff_4 (.T(1'b1), .clk(t_ff_3_qn), .Q(out_4), .reset(in_3));  // open: Qn, preset
endmodule
